// Logisim project ICs.circ as structural Verilog: 6 circuits, main circuit IC 7408 (2-input AND)
module IC_7408__2_input_AND (
  input  in_1,
  input  in_2,
  input  in_3,
  input  in_4,
  input  in_5,
  input  in_6,
  input  in_7,
  input  in_8,
  output out_9,
  output out_10,
  output out_11,
  output out_12
);

  and and_1 (out_9, in_1, in_3);
  and and_2 (out_11, in_5, in_7);
  and and_3 (out_10, in_2, in_4);
  and and_4 (out_12, in_6, in_8);
endmodule

module IC_7432__2_input_OR (
  input  in_1,
  input  in_2,
  input  in_3,
  input  in_4,
  input  in_5,
  input  in_6,
  input  in_7,
  input  in_8,
  output out_9,
  output out_10,
  output out_11,
  output out_12
);

  or or_1 (out_9, in_1, in_3);
  or or_2 (out_11, in_5, in_7);
  or or_3 (out_10, in_2, in_4);
  or or_4 (out_12, in_6, in_8);
endmodule

module IC_7486__2_input_XOR (
  input  in_1,
  input  in_2,
  input  in_3,
  input  in_4,
  input  in_5,
  input  in_6,
  input  in_7,
  input  in_8,
  output out_9,
  output out_10,
  output out_11,
  output out_12
);

  xor xor_1 (out_9, in_1, in_3);
  xor xor_2 (out_11, in_5, in_7);
  xor xor_3 (out_10, in_2, in_4);
  xor xor_4 (out_12, in_6, in_8);
endmodule

module IC_7404__Inverters (
  input  in_1,
  input  in_2,
  input  in_3,
  input  in_4,
  input  in_5,
  input  in_6,
  output out_7,
  output out_8,
  output out_9,
  output out_10,
  output out_11,
  output out_12
);

  not not_1 (out_7, in_1);
  not not_2 (out_9, in_3);
  not not_3 (out_11, in_5);
  not not_4 (out_8, in_2);
  not not_5 (out_10, in_4);
  not not_6 (out_12, in_6);
endmodule

module IC_74153__2x_4_1_MUX (
  input  in_1,
  input  in_2,
  input  in_3,
  input  in_4,
  input  in_5,
  input  in_6,
  input  in_7,
  input  in_8,
  input  in_9,
  input  in_10,
  input  in_11,
  input  in_12,
  output out_13,
  output out_14
);

  wire and_1_out, and_2_out, and_3_out, and_4_out, and_5_out, and_6_out, and_7_out, and_8_out, not_1_out,
       not_2_out, not_3_out, not_4_out;

  not not_1 (not_1_out, in_1);
  not not_2 (not_2_out, in_2);
  not not_3 (not_3_out, in_3);
  not not_4 (not_4_out, in_8);
  and and_1 (and_1_out, in_4, not_3_out, not_2_out, not_1_out);
  and and_2 (and_2_out, in_5, not_3_out, in_2, not_1_out);
  and and_3 (and_3_out, in_6, in_3, not_2_out, not_1_out);
  and and_4 (and_4_out, in_7, in_3, in_2, not_1_out);
  and and_5 (and_5_out, in_9, not_3_out, not_2_out, not_4_out);
  and and_6 (and_6_out, in_10, not_3_out, in_2, not_4_out);
  and and_7 (and_7_out, in_11, in_3, not_2_out, not_4_out);
  and and_8 (and_8_out, in_12, in_3, in_2, not_4_out);
  or or_1 (out_13, and_1_out, and_2_out, and_3_out, and_4_out);
  or or_2 (out_14, and_5_out, and_6_out, and_7_out, and_8_out);
endmodule

module IC_7483__4_bit_Full_Adder (
  input  in_1,
  input  in_2,
  input  in_3,
  input  in_4,
  input  in_5,
  input  in_6,
  input  in_7,
  input  in_8,
  input  in_9,
  input  in_10,
  input  in_11,
  input  in_12,
  output out_13,
  output out_14,
  output out_15,
  output out_16,
  output out_17,
  output out_18,
  output out_19,
  output out_20
);

  wire and_1_out, and_2_out, and_3_out, and_4_out, and_5_out, and_6_out, and_7_out, and_8_out, and_9_out,
       and_10_out, and_11_out, and_12_out;

  ExactlyOne xor_1 (.out(out_13), .in0(in_1), .in1(in_3), .in2(in_5));
  and and_1 (and_1_out, in_1, in_3);
  and and_2 (and_2_out, in_1, in_5);
  and and_3 (and_3_out, in_3, in_5);
  ExactlyOne xor_2 (.out(out_17), .in0(in_7), .in1(in_9), .in2(in_11));
  and and_4 (and_4_out, in_7, in_9);
  and and_5 (and_5_out, in_7, in_11);
  and and_6 (and_6_out, in_9, in_11);
  or or_1 (out_19, and_4_out, and_5_out, and_6_out);
  or or_2 (out_15, and_1_out, and_2_out, and_3_out);
  or or_3 (out_16, and_7_out, and_8_out, and_9_out);
  or or_4 (out_20, and_10_out, and_11_out, and_12_out);
  ExactlyOne xor_3 (.out(out_14), .in0(in_2), .in1(in_4), .in2(in_6));
  and and_7 (and_7_out, in_2, in_4);
  and and_8 (and_8_out, in_2, in_6);
  and and_9 (and_9_out, in_4, in_6);
  ExactlyOne xor_4 (.out(out_18), .in0(in_8), .in1(in_10), .in2(in_12));
  and and_10 (and_10_out, in_8, in_10);
  and and_11 (and_11_out, in_8, in_12);
  and and_12 (and_12_out, in_10, in_12);
endmodule
